// Logisim project ex2.circ as structural Verilog: 1 circuit, main circuit compute_BrUn
module compute_BrUn (
  input  [31:0] INSTRUCTION,
  output BrUn
);

  // AND_Gate and_1 has open pins: in0=7'b1100011, in1=INSTRUCTION[6:0], out=open
  Comparator #(.width(3)) comparator_1 (.a(INSTRUCTION[14:12]), .b(3'b101), .gt(BrUn));  // open: eq, lt
endmodule
